# Fritzing sketch pewpew-lcd-v2 (saved by Fritzing 0.9.9b)
circuit board: 4.11762cm x 6.71789cm
breadboards: 1

parts:
  C2 = Ceramic Capacitor [capacitance=1µF voltage=6.3V package="0603 [SMD, multilayer]"]
  C1 = Ceramic Capacitor [capacitance=1µF voltage=6.3V package="0603 [SMD, multilayer]"]
  U1 = QFN-32 [chip_label=ATSAMD21E18A-MU package=QFN]
  Pad12 = Pad [width=2.4 height=2.4 connect=center]
  X1 = SWITCH_SPDT [package=kps-1290]
  U2 = Voltage Regulator LDO [part_number=AP2112K-3.3TRG1 package=sot23-5]
  -3V = Battery Holders [package=battcon_20mm_4legs]
  breakout = female alternating pin header, 12 pins [form="♀ (female)"]
  GND = Pad [width=3 height=0.37 connect=center]
  Pad11 = Pad [width=3 height=0.37 connect=center]  # not connected
  Pad9 = Pad [width=3 height=0.37 connect=center]
  Pad10 = Pad [width=3 height=0.37 connect=center]
  VUSB = Pad [width=3 height=0.37 connect=center]
  R1 = Resistor [tolerance=±5% resistance=0 power=0.25 package="0603 [SMD]"]
  + = Pad [width=4 height=8.5 connect=center]
  +_2 = Pad [width=4 height=8.5 connect=center]
  U3 = RH-112 Display Out [part_number=RH-112]

nets:
  3.3V: C2.0, U1.9, U1.30, X1.P, breakout.pin1, breakout.pin2, U3.VDD
  GND/usb gnd: C2.1, C1.1, U1.10, U1.28, Pad12.pad, U2.GND, -3V.-, breakout.pin10, breakout.pin11, GND.pad, U3.GND, U3.LED-
  N1: C1.0, U1.29
  left: U1.3
  up: U1.4
  right: U1.5
  down: U1.6
  o: U1.7
  x: U1.8
  N2: U1.11, breakout.pin7
  N3: U1.12, breakout.pin6
  N4: U1.13, breakout.pin5
  N5: U1.14, breakout.pin4
  N6: U1.15, breakout.pin3
  bl: U1.18, R1.Pin_0
  lcd_rst: U1.19, U3.RST
  cs: U1.20, U3.CS
  mosi: U1.21, U3.DIN
  sck: U1.22, U3.CIN
  d-/usb d-: U1.23, Pad9.pad
  d+/usb d+: U1.24, Pad10.pad
  rst: U1.26, breakout.pin12
  swc: U1.31, breakout.pin9
  swd: U1.32, breakout.pin8
  N7: X1.O, U2.OUT
  N8: X1.S, -3V.+, +.pad, +_2.pad
  5V/usb power: U2.IN, U2.EN, VUSB.pad
  N9: R1.Pin_1, U3.LED+

notes:
  http://pewpew.rtfd.io
  R - - 1 2 3 4 5 6 7 + +
  PewPew LCD v2.0
  PewPew LCD, v2.0

custom parts:
  RH-112 Display Out: SH1106 30pin
